# Fritzing sketch DisplayLiFi_with_Arduino_Pro_Mini (saved by Fritzing 0.9.1b)
breadboards: 1

parts:
  パーツ1 = Arduino Pro Mini v13 [part_number=ArduinoProMini]
  IC1 = IC, SIP package, 4 pins [chip_label=Color part_number="S11059-02DT module"]
  R1 = Resistor [tolerance=±5% resistance=2k package=THT]
  R2 = Resistor [tolerance=±5% resistance=2k package=THT]

nets:
  N1: パーツ1.A4, IC1.pin2, R2.Pin_1
  N2: パーツ1.A5, IC1.pin3, R1.Pin_1
  GND: パーツ1.GND, IC1.pin4
  3.3V: パーツ1.VCC, IC1.pin1, R1.Pin_0, R2.Pin_0

notes:
  http://akizukidenshi.com/catalog/g/gK-08316/
